# Fritzing sketch xu4_led (saved by Fritzing 0.9.3b)
breadboards: 1

parts:
  Part1 = ODROID-XU4-SHIFTERSHIELD [part_number="ODROID XU4-SHIFTERSHIELD"]
  LED1 = LED - 5mm [color="Red (633nm)" package="5 mm [THT]"]
  R1 = Resistor [tolerance=±5% resistance=220 package=THT]

nets:
  N1: Part1.GND, R1.Pin_1
  N2: Part1.GPA0.3, LED1.anode
  N3: LED1.cathode, R1.Pin_0

custom parts:
  ODROID-XU4-SHIFTERSHIELD: Odorid XU4-SHIFTERSHIELD by HARDKERNEL
